// Logisim project branch-comp.circ as structural Verilog: 1 circuit, main circuit branch_comp
module branch_comp (
  input  [31:0] BrData1,
  input  [31:0] BrData2,
  input  BrUn,
  output BrEq,
  output BrLt
);

  wire Sign_BrEq, Sign_BrLt, Unsign_BrEq, Unsign_BrLt;

  Comparator #(.width(32)) comparator_1 (.a(BrData1), .b(BrData2), .eq(Sign_BrEq));  // open: gt, lt
  Comparator #(.width(32)) comparator_2 (.a(BrData1), .b(BrData2), .lt(Sign_BrLt));  // open: gt, eq
  Comparator #(.mode("unsigned"), .width(32)) comparator_3 (
    .a(BrData1), .b(BrData2), .eq(Unsign_BrEq));  // open: gt, lt
  Comparator #(.mode("unsigned"), .width(32)) comparator_4 (
    .a(BrData1), .b(BrData2), .lt(Unsign_BrLt));  // open: gt, eq
  Multiplexer multiplexer_1 (.in0(Sign_BrEq), .in1(Unsign_BrEq), .out(BrEq), .sel(BrUn));
  Multiplexer multiplexer_2 (.in0(Sign_BrLt), .in1(Unsign_BrLt), .out(BrLt), .sel(BrUn));

  // Notes on the sheet:
  //   INPUTS to your circuit
  //   DON'T CHANGE THE LOCATIONS OF THE INPUTS AND OUTPUTS!
  //   OUTPUT from your circuit
endmodule
