// Logisim project cpu.circ as structural Verilog: 1 circuit, main circuit cpu
module cpu (
  input  clk,
  input  [31:0] Instruction,
  input  [31:0] MemReadData,
  output [31:0] MemAddress,
  output [31:0] ProgramCounter,
  output [31:0] ra,
  output [31:0] sp,
  output [31:0] t0,
  output [31:0] t1,
  output [31:0] t2,
  output [31:0] s0,
  output [31:0] s1,
  output [31:0] a0,
  output [3:0] MemWriteMask,
  output [31:0] MemWriteData
);

  wire ASel, BrEq, BrLt, BrUn, BSel, MemWEn, PCSel, RegWEn;
  wire [1:0] WBSel;
  wire [2:0] ImmSel;
  wire [3:0] ALUSel;
  wire [31:0] adder_1_out, DataToReg, Immediate, multiplexer_1_out, multiplexer_2_out, multiplexer_3_out,
       multiplexer_4_out, multiplexer_5_out, p_Instruction, p_ProgramCounter, p_ProgramCounterPlus4,
       ProgramCounterPlus4, ReadData1, ReadData2;

  Adder #(.width(32)) adder_1 (.a(ProgramCounter), .b(32'h4), .out(adder_1_out));  // open: cin, cout
  Register #(.width(32)) PC (.D(multiplexer_1_out), .clk(clk), .Q(ProgramCounter));  // open: en, clr
  Multiplexer #(.width(32)) multiplexer_1 (.in0(adder_1_out), .in1(MemAddress), .out(multiplexer_1_out), .sel(PCSel));
  Adder #(.width(32)) adder_2 (.a(ProgramCounter), .b(32'h4), .out(ProgramCounterPlus4));  // open: cin, cout
  Register #(.width(32)) register_1 (.D(ProgramCounterPlus4), .clk(clk), .Q(p_ProgramCounterPlus4));  // open: en, clr
  Register #(.width(32)) register_2 (.D(ProgramCounter), .clk(clk), .Q(p_ProgramCounter));  // open: en, clr
  Register #(.width(32)) register_3 (.D(multiplexer_2_out), .clk(clk), .Q(p_Instruction));  // open: en, clr
  Multiplexer #(.width(32)) multiplexer_2 (.in0(Instruction), .in1(32'h13), .out(multiplexer_2_out), .sel(PCSel));
  control_logic control_logic_1 (
    .PCSel(PCSel), .RegWEn(RegWEn), .ImmSel(ImmSel), .BrUn(BrUn), .ASel(ASel), .BSel(BSel), .ALUSel(ALUSel),
    .MemWEn(MemWEn), .WBSel(WBSel), .Instruction(p_Instruction), .BrEq(BrEq), .BrLt(BrLt));
  Multiplexer #(.select(2), .width(32)) multiplexer_3 (
    .in0(DataToReg), .in1(MemAddress), .in2(p_ProgramCounterPlus4), .out(multiplexer_3_out), .sel(WBSel));  // open: in3
  regfile regfile_1 (
    .ReadIndex1(p_Instruction[19:15]), .ReadIndex2(p_Instruction[24:20]), .WriteIndex(p_Instruction[11:7]),
    .WriteData(multiplexer_3_out), .RegWEn(RegWEn), .clk(clk), .ra(ra), .sp(sp), .t0(t0), .t1(t1), .t2(t2),
    .s0(s0), .s1(s1), .a0(a0), .ReadData1(ReadData1), .ReadData2(ReadData2));
  imm_gen imm_gen_1 (.Instruction(p_Instruction), .ImmSel(ImmSel), .Immediate(Immediate));
  branch_comp branch_comp_1 (.BrData1(ReadData1), .BrData2(ReadData2), .BrUn(BrUn), .BrEq(BrEq), .BrLt(BrLt));
  Multiplexer #(.width(32)) multiplexer_4 (
    .in0(ReadData1), .in1(p_ProgramCounter), .out(multiplexer_4_out), .sel(ASel));
  Multiplexer #(.width(32)) multiplexer_5 (.in0(ReadData2), .in1(Immediate), .out(multiplexer_5_out), .sel(BSel));
  alu alu_1 (.ALUResult(MemAddress), .A(multiplexer_4_out), .B(multiplexer_5_out), .ALUSel(ALUSel));
  partial_load partial_load_1 (
    .Instruction(p_Instruction), .MemAddress(MemAddress), .DataFromMem(MemReadData), .DataToReg(DataToReg));
  partial_store partial_store_1 (
    .Instruction(p_Instruction), .MemAddress(MemAddress), .DataFromReg(ReadData2), .MemWEn(MemWEn),
    .MemWriteMask(MemWriteMask), .DataToMem(MemWriteData));

  // Other names for the same wires on the sheet: ALUResult[31:0] = MemAddress

  // Notes on the sheet:
  //   To IMEM
  //   IMEM (do **NOT** move this)
  //   From IMEM
  //   Inputs/Outputs for testing. Do **NOT** move these.
  //   To DMEM
  //   DMEM (do **NOT** move this)
  //   From DMEM
endmodule
