// Logisim project partial-store.circ as structural Verilog: 1 circuit, main circuit partial_store
module partial_store (
  input  [31:0] Instruction,
  input  [31:0] MemAddress,
  input  [31:0] DataFromReg,
  input  MemWEn,
  output [3:0] MemWriteMask,
  output [31:0] DataToMem
);

  wire comparator_1_eq, comparator_2_eq, comparator_3_eq, comparator_4_eq, comparator_5_eq, comparator_6_eq,
       comparator_7_eq, is_sb, is_sh, is_sw;
  wire [1:0] DataSel, low_2_bits;
  wire [3:0] sb_mask, sh_mask;
  wire [31:0] sb, sh;

  Comparator #(.width(3)) comparator_1 (.a(3'b000), .b(Instruction[14:12]), .eq(comparator_1_eq));  // open: gt, lt
  Comparator #(.width(7)) comparator_2 (.a(7'b0100011), .b(Instruction[6:0]), .eq(comparator_2_eq));  // open: gt, lt
  Comparator #(.width(3)) comparator_3 (.a(3'b001), .b(Instruction[14:12]), .eq(comparator_3_eq));  // open: gt, lt
  Comparator #(.width(7)) comparator_4 (.a(7'b0100011), .b(Instruction[6:0]), .eq(comparator_4_eq));  // open: gt, lt
  Comparator #(.width(3)) comparator_5 (.a(3'b010), .b(Instruction[14:12]), .eq(comparator_5_eq));  // open: gt, lt
  Comparator #(.width(7)) comparator_6 (.a(7'b0100011), .b(Instruction[6:0]), .eq(comparator_6_eq));  // open: gt, lt
  Comparator #(.width(1)) comparator_7 (.a(1'b0), .b(MemWEn), .eq(comparator_7_eq));  // open: gt, lt
  Multiplexer #(.select(2), .width(32)) multiplexer_1 (
    .in0({{24{1'b0}}, DataFromReg[7:0]}), .in1({{16{1'b0}}, DataFromReg[7:0], {8{1'b0}}}),
    .in2({{8{1'b0}}, DataFromReg[7:0], {16{1'b0}}}), .in3({DataFromReg[7:0], {24{1'b0}}}), .out(sb),
    .sel(low_2_bits));
  Multiplexer #(.select(2), .width(4)) multiplexer_2 (
    .in0(4'b0001), .in1(4'b0010), .in2(4'b0100), .in3(4'b1000), .out(sb_mask), .sel(low_2_bits));
  Bit_Extender #(.in_width(32), .out_width(2)) bit_extender_1 (.in(MemAddress), .out(low_2_bits));
  and and_1 (is_sb, comparator_1_eq, comparator_2_eq);
  and and_2 (is_sh, comparator_3_eq, comparator_4_eq);
  and and_3 (is_sw, comparator_5_eq, comparator_6_eq);
  Priority_Encoder #(.select_enc(2)) priority_encoder_1 (
    .in0(is_sb), .in1(is_sh), .in2(is_sw), .in3(comparator_7_eq), .out(DataSel));  // open: gs, en_out, en_in
  Multiplexer #(.select(2), .width(32)) multiplexer_3 (
    .in0({{16{1'b0}}, DataFromReg[15:0]}), .in2({DataFromReg[15:0], {16{1'b0}}}), .out(sh), .sel(low_2_bits));  // open: in1, in3
  Multiplexer #(.select(2), .width(4)) multiplexer_4 (
    .in0(4'b0011), .in2(4'b1100), .out(sh_mask), .sel(low_2_bits));  // open: in1, in3
  Multiplexer #(.select(2), .width(32)) multiplexer_5 (
    .in0(sb), .in1(sh), .in2(DataFromReg), .out(DataToMem), .sel(DataSel));  // open: in3
  Multiplexer #(.select(2), .width(4)) multiplexer_6 (
    .in0(sb_mask), .in1(sh_mask), .in2(4'b1111), .in3(4'b0000), .out(MemWriteMask), .sel(DataSel));

  // Other names for the same wires on the sheet: sb00[7:0] = DataFromReg[7:0]; sb01[15:8] = DataFromReg[7:0];
  //   sb10[23:16] = DataFromReg[7:0]; sb11[31:24] = DataFromReg[7:0]; sh00[15:0] = DataFromReg[15:0];
  //   sh10[31:16] = DataFromReg[15:0]; sw[31:0] = DataFromReg

  // Notes on the sheet:
  //   INPUTS to your circuit
  //   DON'T CHANGE THE LOCATIONS OF THE INPUTS AND OUTPUTS!
  //   OUTPUT from your circuit
endmodule
