// Logisim project regfile.circ as structural Verilog: 1 circuit, main circuit regfile
module regfile (
  input  [4:0] ReadIndex1,
  input  [4:0] ReadIndex2,
  input  [4:0] WriteIndex,
  input  [31:0] WriteData,
  input  RegWEn,
  input  clk,
  output [31:0] ra,
  output [31:0] sp,
  output [31:0] t0,
  output [31:0] t1,
  output [31:0] t2,
  output [31:0] s0,
  output [31:0] s1,
  output [31:0] a0,
  output [31:0] ReadData1,
  output [31:0] ReadData2
);

  wire x0w, x1w, x2w, x3w, x4w, x5w, x6w, x7w, x8w, x9w, x10w, x11w, x12w, x13w, x14w, x15w, x16w, x17w,
       x18w, x19w, x20w, x21w, x22w, x23w, x24w, x25w, x26w, x27w, x28w, x29w, x30w, x31w;
  wire [31:0] multiplexer_1_out, multiplexer_2_out, multiplexer_3_out, multiplexer_4_out, multiplexer_5_out,
       multiplexer_6_out, multiplexer_7_out, multiplexer_8_out, multiplexer_9_out, multiplexer_10_out,
       multiplexer_11_out, multiplexer_12_out, multiplexer_13_out, multiplexer_14_out, multiplexer_15_out,
       multiplexer_16_out, multiplexer_17_out, multiplexer_18_out, multiplexer_19_out, multiplexer_20_out,
       multiplexer_21_out, multiplexer_22_out, multiplexer_23_out, multiplexer_24_out, multiplexer_25_out,
       multiplexer_26_out, multiplexer_27_out, multiplexer_28_out, multiplexer_29_out, multiplexer_30_out,
       multiplexer_31_out, x0d, x0q, x1d, x2d, x3d, x3q, x4d, x4q, x5d, x6d, x7d, x8d, x9d, x10d, x11d, x11q,
       x12d, x12q, x13d, x13q, x14d, x14q, x15d, x15q, x16d, x16q, x17d, x17q, x18d, x18q, x19d, x19q, x20d,
       x20q, x21d, x21q, x22d, x22q, x23d, x23q, x24d, x24q, x25d, x25q, x26d, x26q, x27d, x27q, x28d, x28q,
       x29d, x29q, x30d, x30q, x31d, x31q;

  Multiplexer #(.width(32)) multiplexer_1 (.in0(s0), .in1(x8d), .out(multiplexer_1_out), .sel(x8w));
  Multiplexer #(.width(32)) multiplexer_2 (.in0(x16q), .in1(x16d), .out(multiplexer_2_out), .sel(x16w));
  Multiplexer #(.width(32)) multiplexer_3 (.in0(x24q), .in1(x24d), .out(multiplexer_3_out), .sel(x24w));
  Register #(.width(32)) register_1 (.D(x0q), .en(RegWEn), .clk(clk), .Q(x0q));  // open: clr
  Register #(.width(32)) register_2 (.D(multiplexer_1_out), .en(RegWEn), .clk(clk), .Q(s0));  // open: clr
  Register #(.width(32)) register_3 (.D(multiplexer_2_out), .en(RegWEn), .clk(clk), .Q(x16q));  // open: clr
  Register #(.width(32)) register_4 (.D(multiplexer_3_out), .en(RegWEn), .clk(clk), .Q(x24q));  // open: clr
  Multiplexer #(.width(32)) multiplexer_4 (.in0(ra), .in1(x1d), .out(multiplexer_4_out), .sel(x1w));
  Register #(.width(32)) register_5 (.D(multiplexer_4_out), .en(RegWEn), .clk(clk), .Q(ra));  // open: clr
  Multiplexer #(.width(32)) multiplexer_5 (.in0(s1), .in1(x9d), .out(multiplexer_5_out), .sel(x9w));
  Register #(.width(32)) register_6 (.D(multiplexer_5_out), .en(RegWEn), .clk(clk), .Q(s1));  // open: clr
  Multiplexer #(.width(32)) multiplexer_6 (.in0(x17q), .in1(x17d), .out(multiplexer_6_out), .sel(x17w));
  Register #(.width(32)) register_7 (.D(multiplexer_6_out), .en(RegWEn), .clk(clk), .Q(x17q));  // open: clr
  Multiplexer #(.width(32)) multiplexer_7 (.in0(x25q), .in1(x25d), .out(multiplexer_7_out), .sel(x25w));
  Register #(.width(32)) register_8 (.D(multiplexer_7_out), .en(RegWEn), .clk(clk), .Q(x25q));  // open: clr
  Multiplexer #(.width(32)) multiplexer_8 (.in0(sp), .in1(x2d), .out(multiplexer_8_out), .sel(x2w));
  Register #(.width(32)) register_9 (.D(multiplexer_8_out), .en(RegWEn), .clk(clk), .Q(sp));  // open: clr
  Multiplexer #(.width(32)) multiplexer_9 (.in0(a0), .in1(x10d), .out(multiplexer_9_out), .sel(x10w));
  Register #(.width(32)) register_10 (.D(multiplexer_9_out), .en(RegWEn), .clk(clk), .Q(a0));  // open: clr
  Multiplexer #(.width(32)) multiplexer_10 (.in0(x18q), .in1(x18d), .out(multiplexer_10_out), .sel(x18w));
  Register #(.width(32)) register_11 (.D(multiplexer_10_out), .en(RegWEn), .clk(clk), .Q(x18q));  // open: clr
  Multiplexer #(.width(32)) multiplexer_11 (.in0(x26q), .in1(x26d), .out(multiplexer_11_out), .sel(x26w));
  Register #(.width(32)) register_12 (.D(multiplexer_11_out), .en(RegWEn), .clk(clk), .Q(x26q));  // open: clr
  Multiplexer #(.width(32)) multiplexer_12 (.in0(x3q), .in1(x3d), .out(multiplexer_12_out), .sel(x3w));
  Register #(.width(32)) register_13 (.D(multiplexer_12_out), .en(RegWEn), .clk(clk), .Q(x3q));  // open: clr
  Multiplexer #(.width(32)) multiplexer_13 (.in0(x11q), .in1(x11d), .out(multiplexer_13_out), .sel(x11w));
  Register #(.width(32)) register_14 (.D(multiplexer_13_out), .en(RegWEn), .clk(clk), .Q(x11q));  // open: clr
  Multiplexer #(.width(32)) multiplexer_14 (.in0(x19q), .in1(x19d), .out(multiplexer_14_out), .sel(x19w));
  Register #(.width(32)) register_15 (.D(multiplexer_14_out), .en(RegWEn), .clk(clk), .Q(x19q));  // open: clr
  Multiplexer #(.width(32)) multiplexer_15 (.in0(x27q), .in1(x27d), .out(multiplexer_15_out), .sel(x27w));
  Register #(.width(32)) register_16 (.D(multiplexer_15_out), .en(RegWEn), .clk(clk), .Q(x27q));  // open: clr
  Multiplexer #(.width(32)) multiplexer_16 (.in0(x4q), .in1(x4d), .out(multiplexer_16_out), .sel(x4w));
  Multiplexer #(.width(32)) multiplexer_17 (.in0(x12q), .in1(x12d), .out(multiplexer_17_out), .sel(x12w));
  Multiplexer #(.width(32)) multiplexer_18 (.in0(x20q), .in1(x20d), .out(multiplexer_18_out), .sel(x20w));
  Multiplexer #(.width(32)) multiplexer_19 (.in0(x28q), .in1(x28d), .out(multiplexer_19_out), .sel(x28w));
  Register #(.width(32)) register_17 (.D(multiplexer_16_out), .en(RegWEn), .clk(clk), .Q(x4q));  // open: clr
  Register #(.width(32)) register_18 (.D(multiplexer_17_out), .en(RegWEn), .clk(clk), .Q(x12q));  // open: clr
  Register #(.width(32)) register_19 (.D(multiplexer_18_out), .en(RegWEn), .clk(clk), .Q(x20q));  // open: clr
  Register #(.width(32)) register_20 (.D(multiplexer_19_out), .en(RegWEn), .clk(clk), .Q(x28q));  // open: clr
  Multiplexer #(.width(32)) multiplexer_20 (.in0(t0), .in1(x5d), .out(multiplexer_20_out), .sel(x5w));
  Register #(.width(32)) register_21 (.D(multiplexer_20_out), .en(RegWEn), .clk(clk), .Q(t0));  // open: clr
  Multiplexer #(.width(32)) multiplexer_21 (.in0(x13q), .in1(x13d), .out(multiplexer_21_out), .sel(x13w));
  Register #(.width(32)) register_22 (.D(multiplexer_21_out), .en(RegWEn), .clk(clk), .Q(x13q));  // open: clr
  Multiplexer #(.width(32)) multiplexer_22 (.in0(x21q), .in1(x21d), .out(multiplexer_22_out), .sel(x21w));
  Register #(.width(32)) register_23 (.D(multiplexer_22_out), .en(RegWEn), .clk(clk), .Q(x21q));  // open: clr
  Multiplexer #(.width(32)) multiplexer_23 (.in0(x29q), .in1(x29d), .out(multiplexer_23_out), .sel(x29w));
  Register #(.width(32)) register_24 (.D(multiplexer_23_out), .en(RegWEn), .clk(clk), .Q(x29q));  // open: clr
  Multiplexer #(.width(32)) multiplexer_24 (.in0(t1), .in1(x6d), .out(multiplexer_24_out), .sel(x6w));
  Register #(.width(32)) register_25 (.D(multiplexer_24_out), .en(RegWEn), .clk(clk), .Q(t1));  // open: clr
  Multiplexer #(.width(32)) multiplexer_25 (.in0(x14q), .in1(x14d), .out(multiplexer_25_out), .sel(x14w));
  Register #(.width(32)) register_26 (.D(multiplexer_25_out), .en(RegWEn), .clk(clk), .Q(x14q));  // open: clr
  Multiplexer #(.width(32)) multiplexer_26 (.in0(x22q), .in1(x22d), .out(multiplexer_26_out), .sel(x22w));
  Register #(.width(32)) register_27 (.D(multiplexer_26_out), .en(RegWEn), .clk(clk), .Q(x22q));  // open: clr
  Multiplexer #(.width(32)) multiplexer_27 (.in0(x30q), .in1(x30d), .out(multiplexer_27_out), .sel(x30w));
  Register #(.width(32)) register_28 (.D(multiplexer_27_out), .en(RegWEn), .clk(clk), .Q(x30q));  // open: clr
  Multiplexer #(.width(32)) multiplexer_28 (.in0(t2), .in1(x7d), .out(multiplexer_28_out), .sel(x7w));
  Register #(.width(32)) register_29 (.D(multiplexer_28_out), .en(RegWEn), .clk(clk), .Q(t2));  // open: clr
  Multiplexer #(.width(32)) multiplexer_29 (.in0(x15q), .in1(x15d), .out(multiplexer_29_out), .sel(x15w));
  Register #(.width(32)) register_30 (.D(multiplexer_29_out), .en(RegWEn), .clk(clk), .Q(x15q));  // open: clr
  Multiplexer #(.width(32)) multiplexer_30 (.in0(x23q), .in1(x23d), .out(multiplexer_30_out), .sel(x23w));
  Register #(.width(32)) register_31 (.D(multiplexer_30_out), .en(RegWEn), .clk(clk), .Q(x23q));  // open: clr
  Multiplexer #(.width(32)) multiplexer_31 (.in0(x31q), .in1(x31d), .out(multiplexer_31_out), .sel(x31w));
  Register #(.width(32)) register_32 (.D(multiplexer_31_out), .en(RegWEn), .clk(clk), .Q(x31q));  // open: clr
  Demultiplexer #(.select(5), .width(32)) demultiplexer_1 (
    .out0(x0d), .out1(x1d), .out2(x2d), .out3(x3d), .out4(x4d), .out5(x5d), .out6(x6d), .out7(x7d),
    .out8(x8d), .out9(x9d), .out10(x10d), .out11(x11d), .out12(x12d), .out13(x13d), .out14(x14d),
    .out15(x15d), .out16(x16d), .out17(x17d), .out18(x18d), .out19(x19d), .out20(x20d), .out21(x21d),
    .out22(x22d), .out23(x23d), .out24(x24d), .out25(x25d), .out26(x26d), .out27(x27d), .out28(x28d),
    .out29(x29d), .out30(x30d), .out31(x31d), .in(WriteData), .sel(WriteIndex));
  Demultiplexer #(.select(5)) demultiplexer_2 (
    .out0(x0w), .out1(x1w), .out2(x2w), .out3(x3w), .out4(x4w), .out5(x5w), .out6(x6w), .out7(x7w),
    .out8(x8w), .out9(x9w), .out10(x10w), .out11(x11w), .out12(x12w), .out13(x13w), .out14(x14w),
    .out15(x15w), .out16(x16w), .out17(x17w), .out18(x18w), .out19(x19w), .out20(x20w), .out21(x21w),
    .out22(x22w), .out23(x23w), .out24(x24w), .out25(x25w), .out26(x26w), .out27(x27w), .out28(x28w),
    .out29(x29w), .out30(x30w), .out31(x31w), .in(1'b1), .sel(WriteIndex));
  Multiplexer #(.select(5), .width(32)) multiplexer_32 (
    .in0(x0q), .in1(ra), .in2(sp), .in3(x3q), .in4(x4q), .in5(t0), .in6(t1), .in7(t2), .in8(s0), .in9(s1),
    .in10(a0), .in11(x11q), .in12(x12q), .in13(x13q), .in14(x14q), .in15(x15q), .in16(x16q), .in17(x17q),
    .in18(x18q), .in19(x19q), .in20(x20q), .in21(x21q), .in22(x22q), .in23(x23q), .in24(x24q), .in25(x25q),
    .in26(x26q), .in27(x27q), .in28(x28q), .in29(x29q), .in30(x30q), .in31(x31q), .out(ReadData1),
    .sel(ReadIndex1));
  Multiplexer #(.select(5), .width(32)) multiplexer_33 (
    .in0(x0q), .in1(ra), .in2(sp), .in3(x3q), .in4(x4q), .in5(t0), .in6(t1), .in7(t2), .in8(s0), .in9(s1),
    .in10(a0), .in11(x11q), .in12(x12q), .in13(x13q), .in14(x14q), .in15(x15q), .in16(x16q), .in17(x17q),
    .in18(x18q), .in19(x19q), .in20(x20q), .in21(x21q), .in22(x22q), .in23(x23q), .in24(x24q), .in25(x25q),
    .in26(x26q), .in27(x27q), .in28(x28q), .in29(x29q), .in30(x30q), .in31(x31q), .out(ReadData2),
    .sel(ReadIndex2));

  // Other names for the same wires on the sheet: x1q[31:0] = ra; x2q[31:0] = sp; x5q[31:0] = t0; x6q[31:0] = t1;
  //   x7q[31:0] = t2; x8q[31:0] = s0; x9q[31:0] = s1; x10q[31:0] = a0

  // Notes on the sheet:
  //   INPUTS to your circuit
  //   DON'T CHANGE THE LOCATIONS OF THE INPUTS AND OUTPUTS!
  //   These are DEBUG/TEST outputs from your circuit.
  //   OUTPUTS from your circuit
endmodule
